# Fritzing sketch MCP2221A-3.3V (saved by Fritzing 0.9.4)
breadboards: 1

parts:
  CONN1 = USB connector [package=THT]
  IC1 = IC, DIP package, 14 pins [chip_label=MCP2221A]
  C2 = Ceramic Capacitor [capacitance=0.22µF voltage=16V package="100 mil [THT, multilayer]"]
  C3 = Ceramic Capacitor [capacitance=0.1µF voltage=16V package="100 mil [THT, multilayer]"]
  REG_3_3V = Voltage Regulator - 3.3V [package="TO220 [THT]"]
  C4 = Ceramic Capacitor [capacitance=0.1µF voltage=16V package="100 mil [THT, multilayer]"]
  C5 = Electrolytic Capacitor [capacitance=47µF voltage=35V package="100 mil [THT, electrolytic]"]
  R3 = Resistor [tolerance=±5% resistance=10k package=THT]
  RESET = Pushbutton [package="[THT]"]
  I2C_(3_3V) = female pin header, 2 pins [form="♀ (female)"]
  GPIO_(3_3V) = female pin header, 4 pins [form="♀ (female)"]
  UART_(3_3V) = female pin header, 2 pins [form="♀ (female)"]

nets:
  N1: CONN1.5V, IC1.pin1, REG_3_3V.input_voltage, C4.0, R3.Pin_0
  N2: CONN1.d-, IC1.pin12
  N3: CONN1.d+, IC1.pin13
  GND: CONN1.GND, CONN1.chassis5, CONN1.chassis6, IC1.pin14, C2.0, C3.1, REG_3_3V.GND, C4.1, C5.-, RESET.Pin_3, RESET.Pin_4
  N4: IC1.pin2, GPIO_(3_3V).pin4
  N5: IC1.pin3, GPIO_(3_3V).pin3
  N6: IC1.pin4, C3.0, R3.Pin_1, RESET.Pin_1, RESET.Pin_2
  N7: IC1.pin5, UART_(3_3V).pin1
  N8: IC1.pin6, UART_(3_3V).pin2
  N9: IC1.pin7, GPIO_(3_3V).pin2
  N10: IC1.pin8, GPIO_(3_3V).pin1
  N11: IC1.pin9, I2C_(3_3V).pin2
  N12: IC1.pin10, I2C_(3_3V).pin1
  N13: IC1.pin11, C2.1, REG_3_3V.output_voltage, C5.+

notes:
  D-
  D+
  3.3V
  VBUS
  GND
  ←PC
  SCL
  SDA
  Rx
  Tx
  GP2
  GP3
  GP1
  GP0
