# Fritzing sketch MCP2221A-5V (saved by Fritzing 0.9.4)
breadboards: 1

parts:
  CONN1 = USB connector [package=THT]
  IC1 = IC, DIP package, 14 pins [chip_label=MCP2221A]
  C2 = Ceramic Capacitor [capacitance=0.22µF voltage=16V package="100 mil [THT, multilayer]"]
  C3 = Ceramic Capacitor [capacitance=0.1µF voltage=16V package="100 mil [THT, multilayer]"]
  R3 = Resistor [tolerance=±5% resistance=10k package=THT]
  RESET = Pushbutton [package="[THT]"]
  I2C_(5V) = female pin header, 2 pins [form="♀ (female)"]
  GPIO_(5V) = female pin header, 4 pins [form="♀ (female)"]
  UART_(5V) = female pin header, 2 pins [form="♀ (female)"]

nets:
  N1: CONN1.5V, IC1.pin1, R3.Pin_0
  N2: CONN1.d-, IC1.pin12
  N3: CONN1.d+, IC1.pin13
  N4: CONN1.GND, CONN1.chassis5, CONN1.chassis6, IC1.pin14, C2.0, C3.1, RESET.Pin_3, RESET.Pin_4
  N5: IC1.pin2, GPIO_(5V).pin4
  N6: IC1.pin3, GPIO_(5V).pin3
  N7: IC1.pin4, C3.0, R3.Pin_1, RESET.Pin_1, RESET.Pin_2
  N8: IC1.pin5, UART_(5V).pin1
  N9: IC1.pin6, UART_(5V).pin2
  N10: IC1.pin7, GPIO_(5V).pin2
  N11: IC1.pin8, GPIO_(5V).pin1
  N12: IC1.pin9, I2C_(5V).pin2
  N13: IC1.pin10, I2C_(5V).pin1
  N14: IC1.pin11, C2.1

notes:
  D-
  D+
  VBUS
  GND
  ←PC
  SCL
  SDA
  Rx
  Tx
  GP2
  GP3
  GP1
  GP0
